# Fritzing sketch LCD (saved by Fritzing 0.8.3b)
breadboards: 1

parts:
  Part1 = Arduino Leonardo (Rev3b)
  LCD1 = LCD screen
  R1 = Trimmer Potentiometer [maximum_resistance=10kΩ package=THT]

nets:
  N1: Part1.D2/SDA, LCD1.DB7
  N2: Part1.D3_PWM/SCL, LCD1.DB6
  N3: Part1.D4/A6, LCD1.DB5
  N4: Part1.D5_PWM, LCD1.DB3, LCD1.DB4
  5V: Part1.5V, LCD1.VDD, LCD1.LED+, R1.leg2
  GND: Part1.GND, LCD1.VSS, LCD1.R/W, LCD1.LED-, R1.leg1
  N5: Part1.D11_PWM, LCD1.E
  N6: Part1.D12/A11, LCD1.RS
  N7: LCD1.V0, R1.wiper
