# Fritzing sketch 7segmentaduino (saved by Fritzing 0.8.3b)
breadboards: 1

parts:
  Part1 = Arduino Leonardo (Rev3b)
  7_Segment1 = 7-Segment LED Display [package=THT]
  R1 = Resistor [tolerance=±5% resistance=220 package=THT]
  R2 = Resistor [tolerance=±5% resistance=220 package=THT]
  R3 = Resistor [tolerance=±5% resistance=220 package=THT]
  R4 = Resistor [tolerance=±5% resistance=220 package=THT]
  R5 = Resistor [tolerance=±5% resistance=220 package=THT]
  R6 = Resistor [tolerance=±5% resistance=220 package=THT]
  R7 = Resistor [tolerance=±5% resistance=220 package=THT]

nets:
  N1: Part1.D1/TX, R2.Pin_1
  N2: Part1.D2/SDA, R5.Pin_1
  N3: Part1.D3_PWM/SCL, R3.Pin_1
  N4: Part1.D4/A6, R6.Pin_1
  N5: Part1.D5_PWM, R4.Pin_1
  N6: Part1.D6_PWM/A7, R1.Pin_1
  N7: Part1.D7, R7.Pin_1
  N8: Part1.GND, 7_Segment1.commAnode
  N9: 7_Segment1.cathodeE, R4.Pin_0
  N10: 7_Segment1.cathodeD, R6.Pin_0
  N11: 7_Segment1.cathodeC, R3.Pin_0
  N12: 7_Segment1.cathodeB, R2.Pin_0
  N13: 7_Segment1.cathodeA, R5.Pin_0
  N14: 7_Segment1.cathodeF, R1.Pin_0
  N15: 7_Segment1.cathodeG, R7.Pin_0
