# Fritzing sketch 7segmentaduino4026 (saved by Fritzing 0.8.3b)
breadboards: 1

parts:
  Part1 = Arduino Leonardo (Rev3b)
  7_Segment1 = 7-Segment LED Display [package=THT]
  R1 = Resistor [tolerance=±5% resistance=220 package=THT]
  R2 = Resistor [tolerance=±5% resistance=220 package=THT]
  R3 = Resistor [tolerance=±5% resistance=220 package=THT]
  R4 = Resistor [tolerance=±5% resistance=220 package=THT]
  R5 = Resistor [tolerance=±5% resistance=220 package=THT]
  R6 = Resistor [tolerance=±5% resistance=220 package=THT]
  R7 = Resistor [tolerance=±5% resistance=220 package=THT]
  IC1 = IC, DIP package, 16 pins [chip_label="CD 4026 BE"]

nets:
  N1: Part1.5V, IC1.pin3, IC1.pin16
  N2: Part1.D8/A8, IC1.pin1
  N3: Part1.GND, 7_Segment1.commAnode#2, IC1.pin2, IC1.pin8, IC1.pin15
  N4: 7_Segment1.cathodeE, R4.Pin_0
  N5: 7_Segment1.cathodeD, R6.Pin_0
  N6: 7_Segment1.cathodeC, R3.Pin_0
  N7: 7_Segment1.cathodeB, R2.Pin_0
  N8: 7_Segment1.cathodeA, R5.Pin_0
  N9: 7_Segment1.cathodeF, R1.Pin_0
  N10: 7_Segment1.cathodeG, R7.Pin_0
  N11: R1.Pin_1, IC1.pin6
  N12: R2.Pin_1, IC1.pin10
  N13: R3.Pin_1, IC1.pin13
  N14: R4.Pin_1, IC1.pin11
  N15: R5.Pin_1, IC1.pin12
  N16: R6.Pin_1, IC1.pin9
  N17: R7.Pin_1, IC1.pin7
