# Fritzing sketch czytnik Ir (saved by Fritzing 0.8.4b)
breadboards: 1

parts:
  IR1 = TSOP312.., 314.. [package=THT]
  Part2 = Arduino Leonardo (Rev3b)
  LED1 = LED - 5mm [color="Red (633nm)" package="5 mm [THT]"]
  R1 = Resistor [tolerance=±5% resistance=220 package=THT]
  R2 = Resistor [tolerance=±5% resistance=220 package=THT]

nets:
  N1: IR1.GND, R2.Pin_1
  N2: IR1.Vs, Part2.5V
  N3: IR1.Data, Part2.GND, LED1.cathode
  N4: Part2.D7, R2.Pin_0
  N5: Part2.D10_PWM/A10, R1.Pin_1
  N6: LED1.anode, R1.Pin_0
