# Fritzing sketch RF_TRANS_TEXT (saved by Fritzing 0.8.4b)
breadboards: 1

parts:
  Part1 = Arduino Pro Mini v13
  U1 = RF-LINK_TX [package=rf-link_tx]

nets:
  N1: Part1.GND, U1.ANT
  VCC: Part1.VCC, U1.+5V
  N2: Part1.D9_PWM, U1.GND
