# Fritzing sketch RF_TRANS_GUZIK (saved by Fritzing 0.8.4b)
breadboards: 1

parts:
  Part1 = Arduino Pro Mini v13
  U1 = RF-LINK_TX [package=rf-link_tx]
  S1 = Pushbutton [package="[THT]"]

nets:
  N1: Part1.GND, U1.ANT
  VCC: Part1.VCC, U1.+5V
  N2: Part1.D9_PWM, U1.GND
  N3: Part1.D4, S1.Pin_3, S1.Pin_4
  N4: S1.Pin_1, S1.Pin_2
