# Fritzing sketch RF_recv_GUZIK (saved by Fritzing 0.8.4b)
breadboards: 1

parts:
  R6 = Resistor [package="2512 [SMD]"]
  U3 = RF-LINK_RX [package=rf-link_rx]
  Part1 = Arduino Leonardo (Rev3b)
  LED2 = Super Flux LED blue [color=Blue]

nets:
  N1: R6.Pin_0, LED2.cathode
  N2: R6.Pin_1, U3.ANT, Part1.GND
  N3: Part1.D2/SDA, LED2.anode
