# Fritzing sketch Attiny_standalone (saved by Fritzing 0.8.4b)
breadboards: 1

parts:
  U1 = ATTINY13 [package=dip]
  D1 = Rectifier Diode [part_number=1N4001 package="300 mil [THT]"]
  IR1 = TSOP312.., 314.. [package=THT]
  U2 = RELAY [package=relay-jzc]
  U3 = Luxeon LED [package=luxeon]
  VCC1 = Battery

nets:
  N1: U1.PB3(ADC3), IR1.GND
  N2: U1.PB4(ADC2), D1.anode
  N3: U1.GND, IR1.Data, U2.NC, VCC1.-
  N4: U1.VCC, IR1.Vs, U2.COIL2, VCC1.+
  N5: D1.cathode, U2.NO
  N6: U2.MAIN, U3.C
  N7: U2.COIL1, U3.A

notes:
  230V
