# Fritzing sketch Attiny_wlacznik (saved by Fritzing 0.8.4b)
breadboards: 1

parts:
  Part1 = Arduino Leonardo (Rev3b)
  U1 = ATTINY13 [package=dip]
  D1 = Rectifier Diode [part_number=1N4001 package="300 mil [THT]"]
  IR1 = TSOP312.., 314.. [package=THT]
  U2 = RELAY [package=relay-jzc]
  U3 = Luxeon LED [package=luxeon]

nets:
  N1: Part1.D10_PWM/A10, U1.PB5(NRES)
  N2: U1.PB3(ADC3), IR1.GND
  N3: U1.PB4(ADC2), D1.anode
  N4: D1.cathode, U2.NO
  N5: IR1.Vs, U2.COIL2
  N6: IR1.Data, U2.NC
  N7: U2.MAIN, U3.C
  N8: U2.COIL1, U3.A

notes:
  230V
