# Fritzing sketch Servo (saved by Fritzing 0.8.4b)
breadboards: 1

parts:
  Part1 = Arduino Leonardo (Rev3b)
  J1 = Basic Servo
  R1 = Trimmer Potentiometer [maximum_resistance=10kΩ package=THT]

nets:
  5V: Part1.5V, J1.vcc, R1.leg1
  GND: Part1.GND, J1.gnd, R1.leg2
  N1: Part1.A0, R1.wiper
  N2: Part1.D9_PWM/A9, J1.pulse
