# Fritzing sketch tranzystor (saved by Fritzing 0.8.3b)
breadboards: 1

parts:
  Q1 = NPN-Transistor [package="TO92 [THT]"]
  M1 = DC Motor
  Part1 = Arduino Leonardo (Rev3b)
  D1 = Rectifier Diode [part_number=1N4001 package="300 mil [THT]"]
  R1 = Resistor [tolerance=±5% resistance=220 package=THT]
  D2 = Rectifier Diode [part_number=1N4001 package="300 mil [THT]"]  # not connected

nets:
  N1: Q1.E, Part1.GND
  N2: Q1.B, R1.Pin_0
  N3: Q1.C, M1.pin_1
  N4: Part1.D2/SDA, D1.anode
  N5: D1.cathode, R1.Pin_1
