# Fritzing sketch Multiplexing (saved by Fritzing 0.8.4b)
breadboards: 1

parts:
  LED5 = LED - 5mm [color="Red (633nm)" package="5 mm [THT]"]
  LED6 = LED - 5mm [color="Red (633nm)" package="5 mm [THT]"]
  LED7 = LED - 5mm [color="Red (633nm)" package="5 mm [THT]"]
  LED8 = LED - 5mm [color="Red (633nm)" package="5 mm [THT]"]
  LED9 = LED - 5mm [color="Red (633nm)" package="5 mm [THT]"]
  LED10 = LED - 5mm [color="Red (633nm)" package="5 mm [THT]"]
  LED11 = LED - 5mm [color="Red (633nm)" package="5 mm [THT]"]
  LED12 = LED - 5mm [color="Red (633nm)" package="5 mm [THT]"]
  R1 = Resistor [tolerance=±5% resistance=220 package=THT]
  R2 = Resistor [tolerance=±5% resistance=220 package=THT]
  Part1 = Arduino Leonardo (Rev3b)

nets:
  N1: LED5.cathode, LED6.cathode, LED7.cathode, LED8.cathode, R2.Pin_0
  N2: LED9.cathode, LED10.cathode, LED11.cathode, LED12.cathode, R1.Pin_0
  N3: LED9.anode, Part1.D6_PWM/A7
  N4: LED10.anode, Part1.D5_PWM
  N5: LED11.anode, Part1.D4/A6
  N6: LED12.anode, Part1.D3_PWM/SCL
  N7: R1.Pin_1, Part1.D2/SDA
  N8: R2.Pin_1, Part1.D1/TX
