# Fritzing sketch Kontaktron (saved by Fritzing 0.8.4b)
breadboards: 1
perfboards: 1

parts:
  Part1 = Arduino Leonardo (Rev3b)
  S1 = Reed switch [package=THT]  # not connected
  J1 = Piezo Speaker
  R1 = Trimmer Potentiometer [maximum_resistance=10kΩ package=THT]  # not connected
  IC1 = IC, DIP package, 4 pins [chip_label=IC]  # not connected

nets:
  N1: Part1.D5_PWM, J1.pin2
  N2: Part1.GND, J1.pin1

notes:
  D0 GND VCC
