# Fritzing sketch PCF8574 (saved by Fritzing 0.8.4b)
breadboards: 1

parts:
  U1 = PCF8574 [package="DIP16 [THT]"]
  U2 = PCF8574 [package="DIP16 [THT]"]
  Part1 = Arduino Leonardo (Rev3b)
  R1 = Resistor [tolerance=±5% resistance=220 package=THT]
  R2 = Resistor [tolerance=±5% resistance=220 package=THT]
  R3 = Resistor [tolerance=±5% resistance=220 package=THT]
  R4 = Resistor [tolerance=±5% resistance=220 package=THT]
  LED1 = LED - 5mm [color="Red (633nm)" package="5 mm [THT]"]
  LED2 = LED - 5mm [color="Red (633nm)" package="5 mm [THT]"]
  LED3 = LED - 5mm [color="Blue (505nm)" package="5 mm [THT]"]
  LED4 = LED - 5mm [color="Blue (525nm)" package="5 mm [THT]"]

nets:
  GND: U1.A0, U1.A1, U1.A3, U1.GND, U2.A1, U2.A3, U2.GND, Part1.GND, LED1.cathode, LED2.cathode, LED3.cathode, LED4.cathode
  N1: U1.P3, R2.Pin_0
  N2: U1.P4, R3.Pin_0
  N3: U1.SCL, U2.SCL, Part1.SCL
  N4: U1.SDA, U2.SDA, Part1.D2/SDA, Part1.SDA
  VCC: U1.VCC, U2.A0, U2.VCC, Part1.5V
  N5: U2.P2, R1.Pin_0
  N6: U2.P5, R4.Pin_0
  N7: R1.Pin_1, LED3.anode
  N8: R2.Pin_1, LED2.anode
  N9: R3.Pin_1, LED1.anode
  N10: R4.Pin_1, LED4.anode
