# Fritzing sketch SD (saved by Fritzing 0.8.4b)
breadboards: 1

parts:
  Part1 = Arduino Leonardo (Rev3b)
  U1 = SD_CARD_SOCKET [package=sdcard_4uconn]

nets:
  N1: Part1.D4/A6, U1.DAT0

notes:
  +5V
  CS
  MOSI
  SCK
  MISO
  GND
