# Fritzing sketch Opad_LCD i2c (saved by Fritzing 0.8.4b)
breadboards: 1
perfboards: 2

parts:
  R1 = Trimmer Potentiometer [maximum_resistance=10kΩ package=THT]  # not connected
  U2 = PCF8574 [package="DIP16 [THT]"]  # not connected
  R2 = Resistor [tolerance=±5% resistance=220 package=THT]  # not connected
  LED1 = Super Flux LED blue [color=Blue]  # not connected
  JP1 = Header 2 [package=molex-1x2_lock]  # not connected
  LCD1 = LCD screen  # not connected
  LED2 = Super Flux LED blue [color=Blue]  # not connected
  R3 = Resistor [package="2512 [SMD]"]  # not connected
  R4 = Resistor [package="2512 [SMD]"]  # not connected
  R5 = Resistor [package="2512 [SMD]"]  # not connected
  R6 = Resistor [package="2512 [SMD]"]  # not connected
  JP2 = Header 4 [package=screwterminal-3.5mm-4_lock]
  Part1 = Arduino Leonardo (Rev3b)
  J1 = Piezo Speaker
  U3 = LM393 [package=so08]
  R7 = Trimmer Potentiometer [maximum_resistance=10kΩ package=THT]

nets:
  N1: JP2.1, Part1.SDA
  N2: JP2.2, Part1.SCL
  N3: JP2.3, Part1.5V, U3.G1_V-
  N4: JP2.4, Part1.GND, J1.pin1, U3.G1_+IN
  N5: Part1.A0, U3.G1_-IN
  N6: Part1.D8/A8, U3.G1_OUT
  N7: Part1.D12/A11, J1.pin2
  N8: U3.G2_-IN, R7.leg2
