# Fritzing sketch knight rider (saved by Fritzing 0.8.3b)
breadboards: 1

parts:
  Part1 = Arduino Leonardo (Rev3b)
  LED1 = LED - 5mm [color="Red (633nm)" package="5 mm [THT]"]
  LED2 = LED - 5mm [color="Red (633nm)" package="5 mm [THT]"]
  LED3 = LED - 5mm [color="Red (633nm)" package="5 mm [THT]"]
  LED4 = LED - 5mm [color="Red (633nm)" package="5 mm [THT]"]
  LED5 = LED - 5mm [color="Red (633nm)" package="5 mm [THT]"]
  LED6 = LED - 5mm [color="Red (633nm)" package="5 mm [THT]"]
  LED7 = LED - 5mm [color="Red (633nm)" package="5 mm [THT]"]
  R1 = Resistor [tolerance=±5% resistance=220 package=THT]
  R2 = Resistor [tolerance=±5% resistance=220 package=THT]
  R3 = Resistor [tolerance=±5% resistance=220 package=THT]
  R4 = Resistor [tolerance=±5% resistance=220 package=THT]
  R5 = Resistor [tolerance=±5% resistance=220 package=THT]
  R6 = Resistor [tolerance=±5% resistance=220 package=THT]
  R7 = Resistor [tolerance=±5% resistance=220 package=THT]

nets:
  N1: Part1.D3_PWM/SCL, R4.Pin_1
  N2: Part1.D5_PWM, R3.Pin_1
  N3: Part1.D6_PWM/A7, R2.Pin_1
  N4: Part1.D9_PWM/A9, R5.Pin_1
  N5: Part1.D10_PWM/A10, R1.Pin_1
  N6: Part1.D11_PWM, R6.Pin_1
  N7: Part1.D13_PWM, R7.Pin_1
  N8: Part1.GND, LED1.cathode, LED2.cathode, LED3.cathode, LED4.cathode, LED5.cathode, LED6.cathode, LED7.cathode
  N9: LED1.anode, R5.Pin_0
  N10: LED2.anode, R1.Pin_0
  N11: LED3.anode, R6.Pin_0
  N12: LED4.anode, R2.Pin_0
  N13: LED5.anode, R3.Pin_0
  N14: LED6.anode, R4.Pin_0
  N15: LED7.anode, R7.Pin_0
