# Fritzing sketch Keypad_LCD (saved by Fritzing 0.8.4b)
breadboards: 2
perfboards: 1

parts:
  R1 = Resistor [tolerance=±5% resistance=220 package=THT]
  R2 = Resistor [tolerance=±5% resistance=220 package=THT]
  R3 = Resistor [tolerance=±5% resistance=220 package=THT]
  R4 = Resistor [tolerance=±5% resistance=220 package=THT]
  S1 = Pushbutton [package="[THT]"]
  S2 = Pushbutton [package="[THT]"]
  S3 = Pushbutton [package="[THT]"]
  S4 = Pushbutton [package="[THT]"]
  S5 = Pushbutton [package="[THT]"]
  S6 = Pushbutton [package="[THT]"]
  S7 = Pushbutton [package="[THT]"]
  S8 = Pushbutton [package="[THT]"]
  S9 = Pushbutton [package="[THT]"]
  S10 = Pushbutton [package="[THT]"]
  S12 = Pushbutton [package="[THT]"]
  S13 = Pushbutton [package="[THT]"]
  S14 = Pushbutton [package="[THT]"]
  S15 = Pushbutton [package="[THT]"]
  S16 = Pushbutton [package="[THT]"]
  S17 = Pushbutton [package="[THT]"]
  J1 = male alternating pin header, 8 pins [form="♂ (male)"]  # not connected
  R5 = Resistor [tolerance=±5% resistance=220 package=THT]
  R6 = Resistor [tolerance=±5% resistance=220 package=THT]
  R7 = Resistor [tolerance=±5% resistance=220 package=THT]
  R8 = Resistor [tolerance=±5% resistance=220 package=THT]
  Part1 = Arduino Leonardo (Rev3b)
  Part2 = Arduino Leonardo (Rev3b)
  U2 = Nokia 6100 Color LCD [package=nokia6100_lcd]
  R9 = Resistor [tolerance=±5% resistance=220 package=THT]

nets:
  N1: R1.Pin_0, R2.Pin_1
  N2: R1.Pin_1, Part1.5V, U2.SCK
  N3: R2.Pin_0, R3.Pin_1
  N4: R3.Pin_0, R4.Pin_1
  N5: R4.Pin_0, Part1.GND
  N6: S1.Pin_1, S1.Pin_2, S17.Pin_3, S17.Pin_4
  N7: S1.Pin_3, S1.Pin_4, S16.Pin_3, S16.Pin_4
  N8: S2.Pin_1, S2.Pin_2, S6.Pin_3, S6.Pin_4
  N9: S2.Pin_3, S2.Pin_4, S3.Pin_1, S3.Pin_2
  N10: S3.Pin_3, S3.Pin_4, S14.Pin_1, S14.Pin_2
  N11: S4.Pin_1, S4.Pin_2, S9.Pin_3, S9.Pin_4
  N12: S4.Pin_3, S4.Pin_4, S15.Pin_1, S15.Pin_2
  N13: S5.Pin_1, S5.Pin_2, S8.Pin_3, S8.Pin_4
  N14: S5.Pin_3, S5.Pin_4, S17.Pin_1, S17.Pin_2
  N15: S6.Pin_1, S6.Pin_2, S9.Pin_1, S9.Pin_2
  N16: S7.Pin_1, S7.Pin_2
  N17: S7.Pin_3, S7.Pin_4, S10.Pin_1, S10.Pin_2
  N18: S8.Pin_1, S8.Pin_2
  N19: S10.Pin_3, S10.Pin_4, S12.Pin_1, S12.Pin_2
  N20: S12.Pin_3, S12.Pin_4, S13.Pin_1, S13.Pin_2
  N21: S13.Pin_3, S13.Pin_4, S14.Pin_3, S14.Pin_4
  N22: S15.Pin_3, S15.Pin_4, S16.Pin_1, S16.Pin_2
  N23: R5.Pin_0, R6.Pin_0, R7.Pin_0, R8.Pin_0
  N24: R5.Pin_1, Part1.A1
  N25: R6.Pin_1, Part1.A2
  N26: R7.Pin_1, Part1.A3
  N27: R8.Pin_1, Part1.A4
  N28: Part2.D3_PWM/SCL, U2.DIO
  N29: Part2.D4/A6, U2.RESET
  N30: Part2.D5_PWM, U2.VDIGITAL
  N31: Part2.GND, R9.Pin_1
  N32: U2.CS, R9.Pin_0

notes:
  1
  2
  3
  5
  9
  13
  14
  15
  16
  10
  6
  7
  4
  8
  11
  12
  1  2  3  4 5  6  7  8
