# Fritzing sketch RF_recv_TEXT (saved by Fritzing 0.8.4b)
perfboards: 1
breadboards: 1

parts:
  R1 = Trimmer Potentiometer [maximum_resistance=10kΩ package=THT]  # not connected
  U2 = PCF8574 [package="DIP16 [THT]"]  # not connected
  R2 = Resistor [tolerance=±5% resistance=220 package=THT]  # not connected
  LED1 = Super Flux LED blue [color=Blue]  # not connected
  JP1 = Header 2 [package=molex-1x2_lock]  # not connected
  LCD1 = LCD screen  # not connected
  LED2 = Super Flux LED blue [color=Blue]  # not connected
  R3 = Resistor [package="2512 [SMD]"]  # not connected
  R4 = Resistor [package="2512 [SMD]"]  # not connected
  R5 = Resistor [package="2512 [SMD]"]  # not connected
  R6 = Resistor [package="2512 [SMD]"]  # not connected
  JP2 = Header 4 [package=screwterminal-3.5mm-4_lock]
  U3 = RF-LINK_RX [package=rf-link_rx]
  Part1 = Arduino Leonardo (Rev3b)

nets:
  N1: JP2.1, Part1.SDA
  N2: JP2.2, Part1.SCL
  N3: JP2.3, Part1.5V
  N4: U3.ANT, Part1.GND
