# Fritzing sketch minutnik (saved by Fritzing 0.8.4b)
breadboards: 1

parts:
  Part1 = Arduino Leonardo (Rev3b)
  R1 = Resistor [tolerance=±5% resistance=220 package=THT]
  R2 = Resistor [tolerance=±5% resistance=220 package=THT]
  R3 = Resistor [tolerance=±5% resistance=220 package=THT]
  R4 = Resistor [tolerance=±5% resistance=220 package=THT]
  R5 = Resistor [tolerance=±5% resistance=220 package=THT]
  R6 = Resistor [tolerance=±5% resistance=220 package=THT]
  R7 = Resistor [tolerance=±5% resistance=220 package=THT]
  R8 = Resistor [tolerance=±5% resistance=220 package=THT]
  R9 = Resistor [tolerance=±5% resistance=220 package=THT]
  R10 = Resistor [tolerance=±5% resistance=220 package=THT]
  LED1 = LED - 5mm [color="Red (633nm)" package="5 mm [THT]"]
  LED3 = LED - 5mm [color="Red (633nm)" package="5 mm [THT]"]
  LED4 = LED - 5mm [color="Red (633nm)" package="5 mm [THT]"]
  LED5 = LED - 5mm [color="Red (633nm)" package="5 mm [THT]"]
  LED6 = LED - 5mm [color="Red (633nm)" package="5 mm [THT]"]
  LED7 = LED - 5mm [color="Red (633nm)" package="5 mm [THT]"]
  LED8 = LED - 5mm [color="Red (633nm)" package="5 mm [THT]"]
  LED9 = LED - 5mm [color="Red (633nm)" package="5 mm [THT]"]
  LED10 = LED - 5mm [color="Red (633nm)" package="5 mm [THT]"]
  LED11 = LED - 5mm [color="Red (633nm)" package="5 mm [THT]"]
  J1 = Piezo Speaker
  S2 = Pushbutton [package="[SMD]"]
  S3 = Pushbutton [package="[SMD]"]
  R11 = Resistor [tolerance=±5% resistance=220 package=THT]
  R12 = Resistor [tolerance=±5% resistance=220 package=THT]

nets:
  N1: Part1.D1/TX, Part1.A5, LED1.anode
  N2: Part1.D2/SDA, LED11.anode
  N3: Part1.D3_PWM/SCL, LED10.anode
  N4: Part1.D4/A6, LED9.anode
  N5: Part1.D5_PWM, LED8.anode
  N6: Part1.D6_PWM/A7, LED7.anode
  N7: Part1.D7, LED6.anode
  N8: Part1.5V, S2.Pin_3, S2.Pin_4, S3.Pin_3, S3.Pin_4, R11.Pin_1, R12.Pin_1
  N9: Part1.GND, R1.Pin_0, R2.Pin_0, R3.Pin_0, R4.Pin_0, R5.Pin_0, R6.Pin_0, R7.Pin_0, R8.Pin_0, R9.Pin_0, R10.Pin_0, J1.pin1, R11.Pin_0, R12.Pin_0
  N10: Part1.A4, S3.Pin_1, S3.Pin_2
  N11: Part1.D8/A8, LED5.anode
  N12: Part1.D9_PWM/A9, LED4.anode
  N13: Part1.D10_PWM/A10, LED3.anode
  N14: Part1.D11_PWM, J1.pin2
  N15: Part1.D12/A11, S2.Pin_1, S2.Pin_2
  N16: R1.Pin_1, LED1.cathode
  N17: R2.Pin_1, LED4.cathode
  N18: R3.Pin_1, LED5.cathode
  N19: R4.Pin_1, LED8.cathode
  N20: R5.Pin_1, LED9.cathode
  N21: R6.Pin_1, LED10.cathode
  N22: R7.Pin_1, LED11.cathode
  N23: R8.Pin_1, LED6.cathode
  N24: R9.Pin_1, LED7.cathode
  N25: R10.Pin_1, LED3.cathode
