# Fritzing sketch Keypad_LCD (saved by Fritzing 0.8.4b)
breadboards: 1
perfboards: 1

parts:
  S1 = Pushbutton [package="[THT]"]
  S2 = Pushbutton [package="[THT]"]
  S3 = Pushbutton [package="[THT]"]
  S4 = Pushbutton [package="[THT]"]
  S5 = Pushbutton [package="[THT]"]
  S6 = Pushbutton [package="[THT]"]
  S7 = Pushbutton [package="[THT]"]
  S8 = Pushbutton [package="[THT]"]
  S9 = Pushbutton [package="[THT]"]
  S10 = Pushbutton [package="[THT]"]
  S12 = Pushbutton [package="[THT]"]
  S13 = Pushbutton [package="[THT]"]
  S14 = Pushbutton [package="[THT]"]
  S15 = Pushbutton [package="[THT]"]
  S16 = Pushbutton [package="[THT]"]
  S17 = Pushbutton [package="[THT]"]
  J1 = male alternating pin header, 8 pins [form="♂ (male)"]
  Part1 = Arduino Leonardo (Rev3b)
  S18 = Pushbutton [package="[THT]"]
  R1 = PHOTOCELL [package=photocell]
  R2 = Resistor [tolerance=±5% resistance=1k package=THT]
  LCD1 = LCD screen  # not connected
  J2 = single row smd male pin header, 4 pins [form="♂ (male)"]

nets:
  N1: S1.Pin_1, S1.Pin_2, S17.Pin_3, S17.Pin_4
  N2: S1.Pin_3, S1.Pin_4, S16.Pin_3, S16.Pin_4
  N3: S2.Pin_1, S2.Pin_2, S6.Pin_3, S6.Pin_4
  N4: S2.Pin_3, S2.Pin_4, S3.Pin_1, S3.Pin_2
  N5: S3.Pin_3, S3.Pin_4, S14.Pin_1, S14.Pin_2
  N6: S4.Pin_1, S4.Pin_2, S9.Pin_3, S9.Pin_4
  N7: S4.Pin_3, S4.Pin_4, S15.Pin_1, S15.Pin_2
  N8: S5.Pin_1, S5.Pin_2, S8.Pin_3, S8.Pin_4
  N9: S5.Pin_3, S5.Pin_4, S17.Pin_1, S17.Pin_2
  N10: S6.Pin_1, S6.Pin_2, S9.Pin_1, S9.Pin_2
  N11: S7.Pin_1, S7.Pin_2
  N12: S7.Pin_3, S7.Pin_4, S10.Pin_1, S10.Pin_2
  N13: S8.Pin_1, S8.Pin_2
  N14: S10.Pin_3, S10.Pin_4, S12.Pin_1, S12.Pin_2
  N15: S12.Pin_3, S12.Pin_4, S13.Pin_1, S13.Pin_2
  N16: S13.Pin_3, S13.Pin_4, S14.Pin_3, S14.Pin_4
  N17: S15.Pin_3, S15.Pin_4, S16.Pin_1, S16.Pin_2
  N18: J1.pin1, Part1.D4/A6
  N19: J1.pin2, Part1.D5_PWM
  N20: J1.pin3, Part1.D6_PWM/A7
  N21: J1.pin4, Part1.D7
  N22: J1.pin5, Part1.D8/A8
  N23: J1.pin6, Part1.D9_PWM/A9
  N24: J1.pin7, Part1.D10_PWM/A10
  N25: J1.pin8, Part1.D11_PWM
  N26: Part1.D0/RX, Part1.GND, S18.Pin_1, S18.Pin_2, R1.P$2, J2.pin3
  N27: Part1.IOREF, Part1.5V, R2.Pin_0, J2.pin4
  N28: Part1.A0, R1.P$1, R2.Pin_1
  N29: Part1.SDA, J2.pin1
  N30: Part1.SCL, J2.pin2
  N31: S18.Pin_3, S18.Pin_4

notes:
  *
  8
  5
  0
  #
  D
  C
  B
  A
  7
  9
  4
  1
  2
  6
  3
  1  2  3  4 5  6  7  8
  I2C
