# Fritzing sketch podlewaczka (saved by Fritzing 0.8.4b)
breadboards: 1
perfboards: 3

parts:
  U1 = SHT1x Humdity Sensor [package=sht1x]
  Part1 = Arduino Leonardo (Rev3b)
  LED1 = LED - 5mm [color="Red (633nm)" package="5 mm [THT]"]
  R1 = Resistor [tolerance=±5% resistance=220 package=THT]
  R2 = Resistor [tolerance=±5% resistance=220 package=THT]
  LED2 = LED - 5mm [color="Orange (612nm)" package="5 mm [THT]"]
  LED3 = LED - 5mm [color="Green (565nm)" package="5 mm [THT]"]
  LED4 = LED - 5mm [color="Green (565nm)" package="5 mm [THT]"]
  R3 = Resistor [tolerance=±5% resistance=220 package=THT]
  R4 = Resistor [tolerance=±5% resistance=220 package=THT]
  M1 = DC Motor  # not connected
  U2 = G3VM-61E1 [package=g3vm-61e1]

nets:
  N1: U1.GND, Part1.A2
  N2: U1.DATA, Part1.D7
  N3: U1.SCK, Part1.GND, R1.Pin_1, R3.Pin_1, U2.P$3
  VDD: U1.VDD, Part1.5V, U2.P$2
  N4: Part1.D2/SDA, U2.P$1
  N5: Part1.D8/A8, LED1.anode
  N6: Part1.D9_PWM/A9, LED2.anode
  N7: Part1.D10_PWM/A10, LED3.anode
  N8: Part1.D11_PWM, LED4.anode
  N9: LED1.cathode, R1.Pin_0
  N10: R2.Pin_0, LED2.cathode
  N11: LED3.cathode, R3.Pin_0
  N12: LED4.cathode, R4.Pin_0
