# Fritzing sketch NRF (saved by Fritzing 0.8.4b)

parts:
  Part1 = Arduino Leonardo (Rev3b)
  J1 = double row male pin header, 4 pins [form="♂ (male)"]
  J2 = double row male pin header, 4 pins [form="♂ (male)"]

nets:
  N1: Part1.3V3, J2.pin1
  N2: Part1.GND, J1.pin1
  N3: Part1.D9_PWM/A9, J1.pin2
  N4: Part1.D10_PWM/A10, J2.pin2
