# Fritzing sketch rejestrator (saved by Fritzing 0.8.4b)
breadboards: 1

parts:
  Part1 = Arduino Leonardo (Rev3b)
  U1 = SD_CARD_SOCKET [package=sdcard_4uconn]
  JP3 = Header 4 [package=screwterminal-3.5mm-4_lock]
  LCD1 = LCD screen  # not connected
  Part2 = Real Time Clock Module - DS1307 RTC Breakout Board
  LED1 = RGB LED (com. anode, rbg) [package="5 mm [THT]"]
  R1 = Resistor [tolerance=±5% resistance=220 package=THT]
  U2 = SM130 [package=sm130]
  L1 = Inductor [package="400 mil [THT]"]  # not connected
  L2 = Inductor [package="400 mil [THT]"]  # not connected
  L3 = Inductor [package="400 mil [THT]"]  # not connected
  L4 = Inductor [package="400 mil [THT]"]  # not connected
  L5 = Inductor [package="400 mil [THT]"]  # not connected
  L6 = Inductor [package="400 mil [THT]"]  # not connected
  L7 = Inductor [package="400 mil [THT]"]  # not connected
  L8 = Inductor [package="400 mil [THT]"]  # not connected
  L9 = Inductor [package="400 mil [THT]"]  # not connected
  L10 = Inductor [package="400 mil [THT]"]  # not connected
  L11 = Inductor [package="400 mil [THT]"]  # not connected
  L12 = Inductor [package="400 mil [THT]"]  # not connected
  L13 = Inductor [package="400 mil [THT]"]  # not connected

nets:
  GND: Part1.GND, JP3.4, Part2.GND
  N1: Part1.D8/A8, LED1.green_cathode
  N2: Part1.D9_PWM/A9, LED1.blue_cathode
  N3: Part1.D10_PWM/A10, U1.DAT0
  N4: Part1.SDA, JP3.2
  N5: Part1.SCL, JP3.1, Part2.SCL
  N6: JP3.3, Part2.5V
  N7: LED1.common_anode, R1.Pin_0
  N8: U2.ERROR, U2.RESET, U2.I1, U2.I2, U2.O1, U2.RFGND, U2.ANT1, U2.ANT2

notes:
  +5V
  CS
  MOSI
  SCK
  MISO
  GND
  RFID Antena
  RFID 125kHz
