# Fritzing sketch tvout (saved by Fritzing 0.8.4b)
breadboards: 1

parts:
  Part1 = Arduino Uno (Rev3)
  R1 = Resistor [tolerance=±5% resistance=470 package=THT]
  R2 = Resistor [tolerance=±5% resistance=1k package=THT]
  U1 = Graphical LCD 128x64 [package=lcd-g12864]  # not connected
  JP1 = RCA [package=rca_lock]

nets:
  N1: Part1.GND, JP1.PIN
  N2: Part1.D9_PWM, R2.Pin_1
  N3: Part1.D7, R1.Pin_1
  N4: R1.Pin_0, R2.Pin_0, JP1.SHELL, JP1.SWITCH
