# Fritzing sketch Czujnik alkoholu (saved by Fritzing 0.8.4b)
breadboards: 1

parts:
  Part1 = Arduino Leonardo (Rev3b)
  LCD1 = LCD screen
  VCC1 = 4 x AAA Battery Mount
  U1 = GAS_SENSOR [package=mq-3]
  R1 = Trimmer Potentiometer [maximum_resistance=10kΩ package=THT]
  IC1 = IC, DIP package, 8 pins [chip_label=I2C]

nets:
  N1: Part1.5V, LCD1.RS, IC1.pin4, IC1.pin5
  N2: Part1.GND, LCD1.V0, VCC1.-, U1.A1, R1.wiper, IC1.pin3, IC1.pin6
  N3: Part1.A0, R1.leg1
  N4: Part1.SCL, LCD1.VSS, IC1.pin1, IC1.pin8
  N5: LCD1.VDD, IC1.pin2, IC1.pin7
