# Fritzing sketch Gra Promini (saved by Fritzing 0.8.4b)
breadboards: 1

parts:
  R1 = Resistor [tolerance=±5% resistance=470 package=THT]
  R2 = Resistor [tolerance=±5% resistance=1k package=THT]
  U1 = Graphical LCD 128x64 [package=lcd-g12864]  # not connected
  JP1 = RCA [package=rca_lock]
  SP1 = SPEAKER [package=pcb_mount_speaker]  # not connected
  S1 = Pushbutton [package="[THT]"]
  S2 = Pushbutton [package="[THT]"]
  S3 = Pushbutton [package="[THT]"]
  S4 = Pushbutton [package="[THT]"]
  S5 = Pushbutton [package="[THT]"]
  Part2 = Arduino Pro Mini v13

nets:
  N1: R1.Pin_0, R2.Pin_0, JP1.SHELL, JP1.SWITCH
  N2: R1.Pin_1, Part2.D7
  N3: R2.Pin_1, Part2.D9_PWM
  N4: JP1.PIN, Part2.GND
  N5: S1.Pin_1, S1.Pin_2, Part2.D2
  N6: S1.Pin_3, S1.Pin_4, S2.Pin_1, S2.Pin_2, S3.Pin_1, S3.Pin_2, S4.Pin_1, S4.Pin_2, S5.Pin_1, S5.Pin_2, Part2.D0/TX
  N7: S2.Pin_3, S2.Pin_4, Part2.D3_PWM
  N8: S3.Pin_3, S3.Pin_4, Part2.D4
  N9: S4.Pin_3, S4.Pin_4, Part2.D5_PWM
  N10: S5.Pin_3, S5.Pin_4, Part2.D10_PWM/SS
