# Fritzing sketch Gra UNO (saved by Fritzing 0.8.4b)
breadboards: 1

parts:
  Part1 = Arduino Uno (Rev3)
  R1 = Resistor [tolerance=±5% resistance=470 package=THT]
  R2 = Resistor [tolerance=±5% resistance=1k package=THT]
  U1 = Graphical LCD 128x64 [package=lcd-g12864]  # not connected
  JP1 = RCA [package=rca_lock]
  SP1 = SPEAKER [package=pcb_mount_speaker]  # not connected
  S1 = Pushbutton [package="[THT]"]
  S2 = Pushbutton [package="[THT]"]
  S3 = Pushbutton [package="[THT]"]
  S4 = Pushbutton [package="[THT]"]
  S5 = Pushbutton [package="[THT]"]

nets:
  N1: Part1.GND, JP1.PIN
  N2: Part1.D9_PWM, R2.Pin_1
  N3: Part1.D10_PWM/SS, S5.Pin_3, S5.Pin_4
  N4: Part1.D3_PWM, S2.Pin_3, S2.Pin_4
  N5: Part1.D4, S3.Pin_3, S3.Pin_4
  N6: Part1.D5_PWM, S4.Pin_3, S4.Pin_4
  N7: Part1.D7, R1.Pin_1
  N8: R1.Pin_0, R2.Pin_0, JP1.SHELL, JP1.SWITCH
  N9: S1.Pin_1, S1.Pin_2
  N10: S1.Pin_3, S1.Pin_4, S2.Pin_1, S2.Pin_2, S3.Pin_1, S3.Pin_2, S4.Pin_1, S4.Pin_2, S5.Pin_1, S5.Pin_2
