# Fritzing sketch Akwarium (saved by Fritzing 0.8.4b)
breadboards: 1

parts:
  Part1 = Arduino Leonardo (Rev3b)
  U1 = G3VM-61E1 [package=g3vm-61e1]
  U2 = G3VM-61E1 [package=g3vm-61e1]
  J1 = Basic Servo
  Q1 = NPN-Transistor [package="TO92 [THT]"]
  R1 = Resistor [tolerance=±5% resistance=10k package=THT]
  U3 = TOUCH [package=touch2]
  R2 = Resistor [tolerance=±5% resistance=10 package=THT]

nets:
  N1: Part1.D2/SDA, Q1.B, R1.Pin_0
  N2: Part1.D6_PWM/A7, U2.P$6
  N3: Part1.D7, U3.T1, R2.Pin_1
  5V: Part1.IOREF, Part1.5V, U1.P$5, U2.P$5, J1.vcc, Q1.E, R1.Pin_1, U3.T2
  GND: Part1.GND, U1.P$4, U2.P$4, J1.gnd, Q1.C, R2.Pin_0
  N4: Part1.D8/A8, U1.P$6
  N5: Part1.D9_PWM/A9, J1.pulse

notes:
  DS18B20
  Czujnik poziomu
  Przekaźnik czasowy
  płynów
  do grzałki
  Przekaźnik do pompy
