# Fritzing sketch Modul FM (saved by Fritzing 0.8.4b)
breadboards: 1
stripboards: 1

parts:
  Part1 = Arduino Leonardo (Rev3b)
  IC1 = IC, DIP package, 10 pins [chip_label=TEA5767]
  SPKR1 = Loudspeaker
  IC2 = Dual Op-Amp [part_number=AMP package=so08]
  SPKR2 = Loudspeaker
  C1 = Ceramic Capacitor [capacitance=2.2µF package="100 mil [THT, multilayer]"]
  C2 = Ceramic Capacitor [capacitance=100nF package="100 mil [THT, multilayer]"]
  ANT1 = Antenna  # not connected
  R1 = Rotary Potentiometer (Small) [maximum_resistance=100kΩ package=THT]
  LCD1 = LCD screen  # not connected
  J1 = female pin header, 4 pins [form="♀ (female)"]

nets:
  N1: Part1.5V, IC2.A_-IN, R1.leg2, J1.pin4
  N2: Part1.GND, IC2.A_OUT, R1.leg1, J1.pin3
  N3: Part1.A0, R1.wiper
  N4: Part1.SDA, J1.pin1
  N5: Part1.SCL, J1.pin2
  N6: IC1.pin1, IC1.pin10
  N7: IC1.pin2, IC1.pin9
  N8: IC1.pin3, IC1.pin8
  N9: IC1.pin4, IC1.pin7
  N10: IC1.pin5, IC1.pin6
  N11: SPKR1.pin1, IC2.A_V+
  N12: SPKR1.pin2, IC2.B_OUT
  N13: IC2.A_+IN, C1.0
  N14: IC2.A_V-, C2.0
  N15: IC2.B_+IN, SPKR2.pin2
  N16: IC2.B_-IN, SPKR2.pin1

notes:
  I2C
