# Fritzing sketch Ultrasonic buzzer (saved by Fritzing 0.8.4b)
breadboards: 1

parts:
  Part1 = Arduino Leonardo (Rev3b)
  J1 = Piezo Speaker
  Part2 = Ultrasonic Sensor  # not connected

nets:
  N1: Part1.GND, J1.pin1
  N2: Part1.D9_PWM/A9, J1.pin2
