# Fritzing sketch Untitled Sketch 2 (saved by Fritzing 0.8.4b)
breadboards: 1

parts:
  Part1 = Arduino Pro Mini v13
  Part2 = FTDI Basic Programmer

nets:
  N1: Part1.D0/TX, Part2.RXI
  N2: Part1.D1/RX, Part2.TXO
  N3: Part1.VCC, Part2.POWER
  GND: Part1.GND, Part2.GND
